// Logisim project CPU(Final).circ as structural Verilog: 4 circuits, main circuit 4-bit counter
module _4_bit_counter (
  input  [3:0] Din_3_0,
  input  Clock,
  output [3:0] Dout_3_0
);

  _1_bit_Register u_1_bit_register_1 (.Din(Din_3_0[0]), .Sel(1'b1), .Dout(Dout_3_0[0]), .Clock(Clock));
  _1_bit_Register u_1_bit_register_2 (.Din(Din_3_0[1]), .Sel(1'b1), .Dout(Dout_3_0[1]), .Clock(Clock));
  _1_bit_Register u_1_bit_register_3 (.Din(Din_3_0[2]), .Sel(1'b1), .Dout(Dout_3_0[2]), .Clock(Clock));
  _1_bit_Register u_1_bit_register_4 (.Din(Din_3_0[3]), .Sel(1'b1), .Dout(Dout_3_0[3]), .Clock(Clock));
endmodule

module PC_Adder (
  input  [3:0] Input_Address__3_0,
  output [3:0] Output_Address__3_0
);

  wire [3:0] bit_extender_1_out;

  assign bit_extender_1_out = {{3{1'b0}}, 1'b1};  // Bit_Extender bit_extender_1
  Adder #(.width(4)) adder_1 (
    .a(Input_Address__3_0), .b(bit_extender_1_out), .out(Output_Address__3_0), .cin(1'b0));  // open: cout
endmodule

module CPU_All (
  input  [3:0] Write_Address__3_0,
  input  [16:0] Write_Data__16_0,
  input  Write_Enable,
  input  Clock,
  input  cpu_en
);

  wire alu_1_carry_flag, alu_1_sign_flag, alu_1_zero_flag, CF, cpu_clk, Imm_sel, Jmp_sel, op, Reg_en, SF, ZF;
  wire [3:0] Jmp_add, multiplexer_1_out, n4_bit_counter_1_dout_3_0, pc_adder_1_output_address__3_0;
  wire [4:0] alu_1_r__4_0, multiplexer_2_out, register_set_with_5_5_bit_registers_1_a,
       register_set_with_5_5_bit_registers_1_b;
  wire [16:0] n9x17_sram_1_read_data_1__16_0;

  Multiplexer #(.width(4), .disabled(0), .enable("false")) multiplexer_1 (
    .in0(pc_adder_1_output_address__3_0), .in1(Jmp_add), .out(multiplexer_1_out), .sel(Jmp_sel));
  PC_Adder pc_adder_1 (
    .Input_Address__3_0(n4_bit_counter_1_dout_3_0), .Output_Address__3_0(pc_adder_1_output_address__3_0));
  _4_bit_counter u_4_bit_counter_1 (.Din_3_0(multiplexer_1_out), .Clock(cpu_clk), .Dout_3_0(n4_bit_counter_1_dout_3_0));
  and and_1 (cpu_clk, Clock, cpu_en);
  _9x17_SRAM u_9x17_sram_1 (
    .Write_Data__16_0(Write_Data__16_0), .Write_Enable(Write_Enable),
    .Write_Address__3_0(Write_Address__3_0), .Read_Address_1__3_0(n4_bit_counter_1_dout_3_0),
    .Read_Data_1__16_0({n9x17_sram_1_read_data_1__16_0[16:14], Jmp_add, n9x17_sram_1_read_data_1__16_0[9:0]}),
    .Clock(Clock));  // open: Read_Address_2__3_0, Read_Data_2__16_0
  Register_Set_with_5_5_bit_Registers register_set_with_5_5_bit_registers_1 (
    .Wr(Jmp_add[3:1]), .Ra(Jmp_add[3:1]), .Rb({Jmp_add[0], n9x17_sram_1_read_data_1__16_0[9:8]}),
    .A(register_set_with_5_5_bit_registers_1_a), .B(register_set_with_5_5_bit_registers_1_b),
    .REG_EN(Reg_en), .Wrd(alu_1_r__4_0), .Clock(Clock));
  ALU alu_1 (
    .A__4_0(register_set_with_5_5_bit_registers_1_a), .B_4_0(multiplexer_2_out), .OP(op),
    .Carry_Flag(alu_1_carry_flag), .R__4_0(alu_1_r__4_0), .Sign_Flag(alu_1_sign_flag),
    .Zero_Flag(alu_1_zero_flag));  // open: DIV_Excep
  control_unit control_unit_1 (
    .in_1(n9x17_sram_1_read_data_1__16_0[16:14]), .op(op), .Imm_sel(Imm_sel), .Reg_en(Reg_en), .SF(SF),
    .ZF(ZF), .Jmp_sel(Jmp_sel));
  Multiplexer #(.width(5), .disabled(0), .enable("false")) multiplexer_2 (
    .in0(register_set_with_5_5_bit_registers_1_b), .in1({Jmp_add[0], n9x17_sram_1_read_data_1__16_0[9:6]}),
    .out(multiplexer_2_out), .sel(Imm_sel));
  FLAG_Register flag_register_1 (
    .CF(alu_1_carry_flag), .SF(alu_1_sign_flag), .ZF(alu_1_zero_flag), .Clock(Clock), .ZF_2(CF), .SF_2(SF),
    .ZF_3(ZF));

  // Other names for the same wires on the sheet: clk = Clock

  // Notes on the sheet:
  //   Sub: 01001101100000000      SHL: 01101101100000000 
  //   JGE: 10001100000000000      
  //   Register Mode: 2bits for mode+1 bit for op+3 bits for reg1+3bits for reg2+8bits unused 
  //   Sub: 00001100100000000      SHL: 00100100100000000 
  //   Immediate Mode: 2bits for mode+1 bit for op+3 bits for reg1+5 bits for value+6bits unused 
  //   Branching Mode: 2bits for mode+1 bit for op(for JGE 0)+4 bits for address+10 bits unused 
endmodule

module control_unit (
  input  [2:0] in_1,
  input  SF,
  input  ZF,
  output op,
  output Imm_sel,
  output Reg_en,
  output Jmp_sel
);

  wire Brch_out, Jge_out, not_1_out, not_2_out, not_3_out, not_4_out, not_5_out, or_1_out, Reg_out;

  or or_1 (or_1_out, SF, ZF);
  not not_1 (not_1_out, in_1[1]);
  not not_2 (not_2_out, in_1[0]);
  not not_3 (not_3_out, in_1[2]);
  not not_4 (not_4_out, in_1[2]);
  not not_5 (not_5_out, in_1[1]);
  and Jge (Jge_out, not_2_out, or_1_out);
  and Imm (Imm_sel, not_3_out, in_1[1]);
  and Reg (Reg_out, not_4_out, not_1_out);
  and Brch (Brch_out, in_1[2], not_5_out);
  or or_2 (Reg_en, Imm_sel, Reg_out);
  and and_1 (Jmp_sel, Brch_out, Jge_out);

  assign op = in_1[0];

  // Notes on the sheet:
  //   opcode[2:0]
endmodule
