// Logisim project RAM_library1.circ as structural Verilog: 4 circuits, main circuit 1x1 Static RAM Cell
module _1x1_Static_RAM_Cell (
  input  Read_Select_1,
  input  Read_Select_2,
  input  Write_Data,
  input  Write_Select,
  input  Clock,
  output Read_Data_1,
  output Read_Data_2
);

  wire d_ff_1_q, multiplexer_1_out;

  Multiplexer #(.enable("false")) multiplexer_1 (
    .in0(d_ff_1_q), .in1(Write_Data), .out(multiplexer_1_out), .sel(Write_Select));
  D_Flip_Flop d_ff_1 (.clk(Clock), .D(multiplexer_1_out), .Q(d_ff_1_q));  // open: Qn, preset, en, reset
  and and_1 (Read_Data_1, Read_Select_1, d_ff_1_q);
  and and_2 (Read_Data_2, Read_Select_2, d_ff_1_q);
endmodule

module _1x17_SRAM (
  input  [16:0] Write_Data,
  input  Clock,
  input  Read_Select_1,
  input  Read_Select_2,
  input  Write_Select,
  output [16:0] Read_Data_1,
  output [16:0] Read_Data_2
);

  _1x1_Static_RAM_Cell u_1x1_static_ram_cell_1 (
    .Read_Data_1(Read_Data_1[0]), .Write_Select(Write_Select), .Read_Data_2(Read_Data_2[0]),
    .Read_Select_2(Read_Select_2), .Write_Data(Write_Data[0]), .Read_Select_1(Read_Select_1), .Clock(Clock));
  _1x1_Static_RAM_Cell u_1x1_static_ram_cell_2 (
    .Read_Data_1(Read_Data_1[4]), .Write_Select(Write_Select), .Read_Data_2(Read_Data_2[4]),
    .Read_Select_2(Read_Select_2), .Write_Data(Write_Data[4]), .Read_Select_1(Read_Select_1), .Clock(Clock));
  _1x1_Static_RAM_Cell u_1x1_static_ram_cell_3 (
    .Read_Data_1(Read_Data_1[8]), .Write_Select(Write_Select), .Read_Data_2(Read_Data_2[8]),
    .Read_Select_2(Read_Select_2), .Write_Data(Write_Data[8]), .Read_Select_1(Read_Select_1), .Clock(Clock));
  _1x1_Static_RAM_Cell u_1x1_static_ram_cell_4 (
    .Read_Data_1(Read_Data_1[12]), .Write_Select(Write_Select), .Read_Data_2(Read_Data_2[12]),
    .Read_Select_2(Read_Select_2), .Write_Data(Write_Data[12]), .Read_Select_1(Read_Select_1), .Clock(Clock));
  _1x1_Static_RAM_Cell u_1x1_static_ram_cell_5 (
    .Read_Data_1(Read_Data_1[16]), .Write_Select(Write_Select), .Read_Data_2(Read_Data_2[16]),
    .Read_Select_2(Read_Select_2), .Write_Data(Write_Data[16]), .Read_Select_1(Read_Select_1), .Clock(Clock));
  _1x1_Static_RAM_Cell u_1x1_static_ram_cell_6 (
    .Read_Data_1(Read_Data_1[1]), .Write_Select(Write_Select), .Read_Data_2(Read_Data_2[1]),
    .Read_Select_2(Read_Select_2), .Write_Data(Write_Data[1]), .Read_Select_1(Read_Select_1), .Clock(Clock));
  _1x1_Static_RAM_Cell u_1x1_static_ram_cell_7 (
    .Read_Data_1(Read_Data_1[5]), .Write_Select(Write_Select), .Read_Data_2(Read_Data_2[5]),
    .Read_Select_2(Read_Select_2), .Write_Data(Write_Data[5]), .Read_Select_1(Read_Select_1), .Clock(Clock));
  _1x1_Static_RAM_Cell u_1x1_static_ram_cell_8 (
    .Read_Data_1(Read_Data_1[9]), .Write_Select(Write_Select), .Read_Data_2(Read_Data_2[9]),
    .Read_Select_2(Read_Select_2), .Write_Data(Write_Data[9]), .Read_Select_1(Read_Select_1), .Clock(Clock));
  _1x1_Static_RAM_Cell u_1x1_static_ram_cell_9 (
    .Read_Data_1(Read_Data_1[13]), .Write_Select(Write_Select), .Read_Data_2(Read_Data_2[13]),
    .Read_Select_2(Read_Select_2), .Write_Data(Write_Data[13]), .Read_Select_1(Read_Select_1), .Clock(Clock));
  _1x1_Static_RAM_Cell u_1x1_static_ram_cell_10 (
    .Read_Data_1(Read_Data_1[2]), .Write_Select(Write_Select), .Read_Data_2(Read_Data_2[2]),
    .Read_Select_2(Read_Select_2), .Write_Data(Write_Data[2]), .Read_Select_1(Read_Select_1), .Clock(Clock));
  _1x1_Static_RAM_Cell u_1x1_static_ram_cell_11 (
    .Read_Data_1(Read_Data_1[6]), .Write_Select(Write_Select), .Read_Data_2(Read_Data_2[6]),
    .Read_Select_2(Read_Select_2), .Write_Data(Write_Data[6]), .Read_Select_1(Read_Select_1), .Clock(Clock));
  _1x1_Static_RAM_Cell u_1x1_static_ram_cell_12 (
    .Read_Data_1(Read_Data_1[10]), .Write_Select(Write_Select), .Read_Data_2(Read_Data_2[10]),
    .Read_Select_2(Read_Select_2), .Write_Data(Write_Data[10]), .Read_Select_1(Read_Select_1), .Clock(Clock));
  _1x1_Static_RAM_Cell u_1x1_static_ram_cell_13 (
    .Read_Data_1(Read_Data_1[14]), .Write_Select(Write_Select), .Read_Data_2(Read_Data_2[14]),
    .Read_Select_2(Read_Select_2), .Write_Data(Write_Data[14]), .Read_Select_1(Read_Select_1), .Clock(Clock));
  _1x1_Static_RAM_Cell u_1x1_static_ram_cell_14 (
    .Read_Data_1(Read_Data_1[3]), .Write_Select(Write_Select), .Read_Data_2(Read_Data_2[3]),
    .Read_Select_2(Read_Select_2), .Write_Data(Write_Data[3]), .Read_Select_1(Read_Select_1), .Clock(Clock));
  _1x1_Static_RAM_Cell u_1x1_static_ram_cell_15 (
    .Read_Data_1(Read_Data_1[7]), .Write_Select(Write_Select), .Read_Data_2(Read_Data_2[7]),
    .Read_Select_2(Read_Select_2), .Write_Data(Write_Data[7]), .Read_Select_1(Read_Select_1), .Clock(Clock));
  _1x1_Static_RAM_Cell u_1x1_static_ram_cell_16 (
    .Read_Data_1(Read_Data_1[11]), .Write_Select(Write_Select), .Read_Data_2(Read_Data_2[11]),
    .Read_Select_2(Read_Select_2), .Write_Data(Write_Data[11]), .Read_Select_1(Read_Select_1), .Clock(Clock));
  _1x1_Static_RAM_Cell u_1x1_static_ram_cell_17 (
    .Read_Data_1(Read_Data_1[15]), .Write_Select(Write_Select), .Read_Data_2(Read_Data_2[15]),
    .Read_Select_2(Read_Select_2), .Write_Data(Write_Data[15]), .Read_Select_1(Read_Select_1), .Clock(Clock));

  // Other names for the same wires on the sheet: CLK = Clock; RD1_0 = Read_Data_1[0]; RD1_1 = Read_Data_1[1];
  //   RD1_2 = Read_Data_1[2]; RD1_3 = Read_Data_1[3]; RD1_4 = Read_Data_1[4]; RD1_5 = Read_Data_1[5];
  //   RD1_6 = Read_Data_1[6]; RD1_7 = Read_Data_1[7]; RD1_8 = Read_Data_1[8]; RD1_9 = Read_Data_1[9];
  //   RD1_10 = Read_Data_1[10]; RD1_11 = Read_Data_1[11]; RD1_12 = Read_Data_1[12]; RD1_13 = Read_Data_1[13];
  //   RD1_14 = Read_Data_1[14]; RD1_15 = Read_Data_1[15]; RD1_16 = Read_Data_1[16]; RD2_0 = Read_Data_2[0];
  //   RD2_1 = Read_Data_2[1]; RD2_2 = Read_Data_2[2]; RD2_3 = Read_Data_2[3]; RD2_4 = Read_Data_2[4];
  //   RD2_5 = Read_Data_2[5]; RD2_6 = Read_Data_2[6]; RD2_7 = Read_Data_2[7]; RD2_8 = Read_Data_2[8];
  //   RD2_9 = Read_Data_2[9]; RD2_10 = Read_Data_2[10]; RD2_11 = Read_Data_2[11]; RD2_12 = Read_Data_2[12];
  //   RD2_13 = Read_Data_2[13]; RD2_14 = Read_Data_2[14]; RD2_15 = Read_Data_2[15]; RD2_16 = Read_Data_2[16];
  //   RS1 = Read_Select_1; RS2 = Read_Select_2; D0 = Write_Data[0]; D1 = Write_Data[1]; D2 = Write_Data[2];
  //   D3 = Write_Data[3]; D4 = Write_Data[4]; D5 = Write_Data[5]; D6 = Write_Data[6]; D7 = Write_Data[7];
  //   D8 = Write_Data[8]; D9 = Write_Data[9]; D10 = Write_Data[10]; D11 = Write_Data[11]; D12 = Write_Data[12];
  //   D13 = Write_Data[13]; D14 = Write_Data[14]; D15 = Write_Data[15]; D16 = Write_Data[16]; WS = Write_Select
endmodule

module _9x17_SRAM (
  input  [16:0] Write_Data__16_0,
  input  Write_Enable,
  input  [3:0] Write_Address__3_0,
  input  [3:0] Read_Address_1__3_0,
  input  [3:0] Read_Address_2__3_0,
  input  Clock,
  output [16:0] Read_Data_1__16_0,
  output [16:0] Read_Data_2__16_0
);

  wire R1_0, R1_1, R1_2, R1_3, R1_4, R1_5, R1_6, R1_7, R1_8, R2_0, R2_0_t, R2_1, R2_1_t, R2_2, R2_3, R2_4,
       R2_5, R2_6, R2_7, R2_8, undriven, undriven_2, W0, W1, W2, W3, W4, W5, W6, W7, W8;
  wire [16:0] RD1_0, RD1_1, RD1_2, RD1_3, RD1_4, RD1_5, RD1_6, RD1_7, RD1_8, RD2_0, RD2_1, RD2_2, RD2_3,
       RD2_4, RD2_5, RD2_6, RD2_7, RD2_8;

  Decoder #(.select(4), .disabled(0)) decoder_1 (
    .out0(W0), .out1(W1), .out2(W2), .out3(W3), .out4(W4), .out5(W5), .out6(W6), .out7(W7), .out8(W8),
    .sel(Write_Address__3_0), .en(Write_Enable));  // open: out9, out10, out11, out12, out13, out14, out15
  Decoder #(.select(4), .disabled(0)) decoder_2 (
    .out0(R1_0), .out1(R1_1), .out2(R1_2), .out3(R1_3), .out4(R1_4), .out5(R1_5), .out6(R1_6), .out7(R1_7),
    .out8(R1_8), .sel(Read_Address_1__3_0), .en(undriven));  // open: out9, out10, out11, out12, out13, out14, out15
  Decoder #(.select(4), .disabled(0)) decoder_3 (
    .out0(R2_0_t), .out1(R2_1_t), .out2(R2_2), .out3(R2_3), .out4(R2_4), .out5(R2_5), .out6(R2_6),
    .out7(R2_7), .out8(R2_8), .sel(Read_Address_2__3_0), .en(undriven_2));  // open: out9, out10, out11, out12, out13, out14, out15
  _1x17_SRAM u_1x17_sram_1 (
    .Read_Select_2(R2_0), .Read_Select_1(R1_0), .Write_Data(Write_Data__16_0), .Read_Data_1(RD1_0),
    .Write_Select(W0), .Clock(Clock), .Read_Data_2(RD2_0));
  _1x17_SRAM u_1x17_sram_2 (
    .Read_Select_2(R2_1), .Read_Select_1(R1_1), .Write_Data(Write_Data__16_0), .Read_Data_1(RD1_1),
    .Write_Select(W1), .Clock(Clock), .Read_Data_2(RD2_1));
  _1x17_SRAM u_1x17_sram_3 (
    .Read_Select_2(R2_2), .Read_Select_1(R1_2), .Write_Data(Write_Data__16_0), .Read_Data_1(RD1_2),
    .Write_Select(W2), .Clock(Clock), .Read_Data_2(RD2_2));
  _1x17_SRAM u_1x17_sram_4 (
    .Read_Select_2(R2_3), .Read_Select_1(R1_3), .Write_Data(Write_Data__16_0), .Read_Data_1(RD1_3),
    .Write_Select(W3), .Clock(Clock), .Read_Data_2(RD2_3));
  _1x17_SRAM u_1x17_sram_5 (
    .Read_Select_2(R2_4), .Read_Select_1(R1_4), .Write_Data(Write_Data__16_0), .Read_Data_1(RD1_4),
    .Write_Select(W4), .Clock(Clock), .Read_Data_2(RD2_4));
  _1x17_SRAM u_1x17_sram_6 (
    .Read_Select_2(R2_5), .Read_Select_1(R1_5), .Write_Data(Write_Data__16_0), .Read_Data_1(RD1_5),
    .Write_Select(W5), .Clock(Clock), .Read_Data_2(RD2_5));
  _1x17_SRAM u_1x17_sram_7 (
    .Read_Select_2(R2_6), .Read_Select_1(R1_6), .Write_Data(Write_Data__16_0), .Read_Data_1(RD1_6),
    .Write_Select(W6), .Clock(Clock), .Read_Data_2(RD2_6));
  _1x17_SRAM u_1x17_sram_8 (
    .Read_Select_2(R2_7), .Read_Select_1(R1_7), .Write_Data(Write_Data__16_0), .Read_Data_1(RD1_7),
    .Write_Select(W7), .Clock(Clock), .Read_Data_2(RD2_7));
  _1x17_SRAM u_1x17_sram_9 (
    .Read_Select_2(R2_8), .Read_Select_1(R1_8), .Write_Data(Write_Data__16_0), .Read_Data_1(RD1_8),
    .Write_Select(W8), .Clock(Clock), .Read_Data_2(RD2_8));
  assign Read_Data_1__16_0 = RD1_0 | RD1_1 | RD1_2 | RD1_3 | RD1_4 | RD1_5 | RD1_6 | RD1_7 | RD1_8;  // OR_Gate or_1, 17 bits wide
  assign Read_Data_2__16_0 = RD2_0 | RD2_1 | RD2_2 | RD2_3 | RD2_4 | RD2_5 | RD2_6 | RD2_7 | RD2_8;  // OR_Gate or_2, 17 bits wide
endmodule

module RAM_testing (
  input  [3:0] Read_Address_1__3_0,
  input  [3:0] Read_Address_1__3_0_2,
  input  [3:0] Write_Address__3_0,
  input  [16:0] Write_Data__16_0,
  input  Write_Enable,
  input  Clock,
  output [16:0] Read_Data_1__16_0,
  output [16:0] Read_Data_2__16_0
);

  _9x17_SRAM u_9x17_sram_1 (
    .Write_Data__16_0(Write_Data__16_0), .Write_Enable(Write_Enable),
    .Write_Address__3_0(Write_Address__3_0), .Read_Address_1__3_0(Read_Address_1__3_0),
    .Read_Address_2__3_0(Read_Address_1__3_0_2), .Read_Data_1__16_0(Read_Data_1__16_0),
    .Read_Data_2__16_0(Read_Data_2__16_0), .Clock(Clock));
endmodule
