// Logisim project Register_Set_Library.circ as structural Verilog: 6 circuits, main circuit 1-bit Register
module _1_bit_Register (
  input  Din,
  input  Sel,
  input  Clock,
  output Dout
);

  wire n1_bit_2to1_mux_1_out;

  _1_bit_2to1_MUX u_1_bit_2to1_mux_1 (.A(Dout), .Sel(Sel), .B(Din), .Out(n1_bit_2to1_mux_1_out));
  D_Flip_Flop d_ff_1 (.clk(Clock), .D(n1_bit_2to1_mux_1_out), .Q(Dout));  // open: Qn, preset, en, reset
endmodule

module _1_bit_2to1_MUX (
  input  A,
  input  Sel,
  input  B,
  output Out
);

  wire and_1_out, and_2_out, not_1_out;

  not not_1 (not_1_out, Sel);
  and and_1 (and_1_out, A, not_1_out);
  and and_2 (and_2_out, Sel, B);
  or or_1 (Out, and_1_out, and_2_out);
endmodule

module _5_bit_Register (
  input  [4:0] Din_4_0,
  input  Sel,
  input  Clock,
  output [4:0] Dout_4_0
);

  _1_bit_Register u_1_bit_register_1 (.Din(Din_4_0[0]), .Sel(Sel), .Dout(Dout_4_0[0]), .Clock(Clock));
  _1_bit_Register u_1_bit_register_2 (.Din(Din_4_0[1]), .Sel(Sel), .Dout(Dout_4_0[1]), .Clock(Clock));
  _1_bit_Register u_1_bit_register_3 (.Din(Din_4_0[2]), .Sel(Sel), .Dout(Dout_4_0[2]), .Clock(Clock));
  _1_bit_Register u_1_bit_register_4 (.Din(Din_4_0[3]), .Sel(Sel), .Dout(Dout_4_0[3]), .Clock(Clock));
  _1_bit_Register u_1_bit_register_5 (.Din(Din_4_0[4]), .Sel(Sel), .Dout(Dout_4_0[4]), .Clock(Clock));
endmodule

module Register_Set_with_5_5_bit_Registers (
  input  REG_EN,
  input  [2:0] Wr,
  input  [4:0] Wrd,
  input  Clock,
  input  [2:0] Ra,
  input  [2:0] Rb,
  output [4:0] A,
  output [4:0] B
);

  wire Reg0, Reg1, Reg2, Reg3, Reg4;
  wire [4:0] R0, R1, R2, R3, R4;

  Decoder #(.select(3)) decoder_1 (
    .out0(Reg0), .out1(Reg1), .out2(Reg2), .out3(Reg3), .out4(Reg4), .sel(Wr), .en(REG_EN));  // open: out5, out6, out7
  _5_bit_Register Register_0 (.Din_4_0(Wrd), .Sel(Reg0), .Clock(Clock), .Dout_4_0(R0));
  _5_bit_Register Register_1 (.Din_4_0(Wrd), .Sel(Reg1), .Clock(Clock), .Dout_4_0(R1));
  _5_bit_Register Register_2 (.Din_4_0(Wrd), .Sel(Reg2), .Clock(Clock), .Dout_4_0(R2));
  _5_bit_Register Register_3 (.Din_4_0(Wrd), .Sel(Reg3), .Clock(Clock), .Dout_4_0(R3));
  _5_bit_Register Register_4 (.Din_4_0(Wrd), .Sel(Reg4), .Clock(Clock), .Dout_4_0(R4));
  Multiplexer #(.select(3), .width(5), .enable("false")) multiplexer_1 (
    .in0(R0), .in1(R1), .in2(R2), .in3(R3), .in4(R4), .out(A), .sel(Ra));  // open: in5, in6, in7
  Multiplexer #(.select(3), .width(5), .enable("false")) multiplexer_2 (
    .in0(R0), .in1(R1), .in2(R2), .in3(R3), .in4(R4), .out(B), .sel(Rb));  // open: in5, in6, in7
endmodule

module FLAG_Register (
  input  CF,
  input  SF,
  input  ZF,
  input  Clock,
  output ZF_2,
  output SF_2,
  output ZF_3
);

  _1_bit_Register u_1_bit_register_1 (.Din(CF), .Sel(1'b1), .Dout(ZF_2), .Clock(Clock));
  _1_bit_Register u_1_bit_register_2 (.Din(SF), .Sel(1'b1), .Dout(SF_2), .Clock(Clock));
  _1_bit_Register u_1_bit_register_3 (.Din(ZF), .Sel(1'b1), .Dout(ZF_3), .Clock(Clock));
endmodule

module Register_Set_Testing (
  input  [2:0] Ra__2_0,
  input  [2:0] Rb__2_0,
  input  REG_EN,
  input  [2:0] Wr__2_0,
  input  [4:0] Wrd__4_0,
  output [4:0] A__4_0,
  output [4:0] B__4_0
);

  wire Clock_out;

  Clock Clock (.out(Clock_out));
  Register_Set_with_5_5_bit_Registers register_set_with_5_5_bit_registers_1 (
    .Wr(Wr__2_0), .Ra(Ra__2_0), .Rb(Rb__2_0), .A(A__4_0), .B(B__4_0), .REG_EN(REG_EN), .Wrd(Wrd__4_0),
    .Clock(Clock_out));
endmodule
