// Logisim project final.circ as structural Verilog: 5 circuits, main circuit 5-bit Adder/Subtractor
module _5_bit_Adder_Subtractor (
  input  [4:0] A,
  input  [4:0] B,
  output [4:0] O,
  output Carry
);

  wire fa_1_cout, fa_2_cout, fa_3_cout, fa_4_cout, fa_5_cout, not_1_out, xor_1_out, xor_2_out, xor_3_out,
       xor_4_out, xor_5_out;

  not not_1 (not_1_out, 1'b0);
  xor xor_1 (xor_1_out, B[4], not_1_out);
  not not_2 (Carry, fa_1_cout);
  FA fa_1 (.a(xor_1_out), .b(A[4]), .Cin(fa_2_cout), .S(O[4]), .Cout(fa_1_cout));
  xor xor_2 (xor_2_out, B[3], not_1_out);
  FA fa_2 (.a(xor_2_out), .b(A[3]), .Cin(fa_3_cout), .S(O[3]), .Cout(fa_2_cout));
  xor xor_3 (xor_3_out, B[2], not_1_out);
  FA fa_3 (.a(xor_3_out), .b(A[2]), .Cin(fa_4_cout), .S(O[2]), .Cout(fa_3_cout));
  xor xor_4 (xor_4_out, B[1], not_1_out);
  FA fa_4 (.a(xor_4_out), .b(A[1]), .Cin(fa_5_cout), .S(O[1]), .Cout(fa_4_cout));
  xor xor_5 (xor_5_out, B[0], not_1_out);
  FA fa_5 (.a(xor_5_out), .b(A[0]), .Cin(not_1_out), .S(O[0]), .Cout(fa_5_cout));
endmodule

module FA (
  input  a,
  input  b,
  input  Cin,
  output S,
  output Cout
);

  wire and_1_out, and_2_out, xor_1_out;

  xor xor_1 (xor_1_out, a, b);
  xor xor_2 (S, xor_1_out, Cin);
  and and_1 (and_1_out, Cin, xor_1_out);
  and and_2 (and_2_out, a, b);
  or or_1 (Cout, and_1_out, and_2_out);
endmodule

module _5_bit_Left_Shifter (
  input  [4:0] A,
  input  [2:0] Shift,
  output [4:0] O
);

  Multiplexer #(.select(3), .enable("false")) multiplexer_1 (
    .in0(A[4]), .in1(A[3]), .in2(A[2]), .in3(A[1]), .in4(A[0]), .out(O[4]), .sel(Shift));  // open: in5, in6, in7
  Multiplexer #(.select(3), .enable("false")) multiplexer_2 (
    .in0(A[3]), .in1(A[2]), .in2(A[1]), .in3(A[0]), .in4(1'b0), .out(O[3]), .sel(Shift));  // open: in5, in6, in7
  Multiplexer #(.select(3), .enable("false")) multiplexer_3 (
    .in0(A[2]), .in1(A[1]), .in2(A[0]), .in3(1'b0), .in4(1'b0), .out(O[2]), .sel(Shift));  // open: in5, in6, in7
  Multiplexer #(.select(3), .enable("false")) multiplexer_4 (
    .in0(A[1]), .in1(A[0]), .in2(1'b0), .in3(1'b0), .in4(1'b0), .out(O[1]), .sel(Shift));  // open: in5, in6, in7
  Multiplexer #(.select(3), .enable("false")) multiplexer_5 (
    .in0(A[0]), .in1(1'b0), .in2(1'b0), .in3(1'b0), .in4(1'b0), .out(O[0]), .sel(Shift));  // open: in5, in6, in7
endmodule

module ALU (
  input  [4:0] A__4_0,
  input  [4:0] B_4_0,
  input  OP,
  output Carry_Flag,
  output [4:0] R__4_0,
  output Sign_Flag,
  output Zero_Flag,
  output DIV_Excep
);

  wire or_1_out;
  wire [4:0] L_SHIFT, Sub;

  _5_bit_Adder_Subtractor u_5_bit_adder_subtractor_1 (.A(A__4_0), .B(B_4_0), .O(Sub), .Carry(Carry_Flag));
  _5_bit_Left_Shifter u_5_bit_left_shifter_1 (.A(A__4_0), .O(L_SHIFT), .Shift(B_4_0[4:2]));
  Multiplexer #(.width(5), .enable("false")) multiplexer_1 (.in0(Sub), .in1(L_SHIFT), .out(R__4_0), .sel(OP));
  or or_1 (or_1_out, R__4_0[4], R__4_0[3], R__4_0[2], R__4_0[1], R__4_0[0]);
  not not_1 (Zero_Flag, or_1_out);

  assign Sign_Flag = R__4_0[4];

  // Other names for the same wires on the sheet: A[4:0] = A__4_0; B[4:0] = B_4_0; Shift[2:0] = B_4_0[4:2]
endmodule

module ALU_testing (
  input  [4:0] A,
  input  [4:0] B,
  input  OP,
  output [4:0] R,
  output CF,
  output SF,
  output ZF
);

  ALU alu_1 (
    .A__4_0(A), .B_4_0(B), .OP(OP), .Carry_Flag(CF), .R__4_0(R), .Sign_Flag(SF), .Zero_Flag(ZF));  // open: DIV_Excep
endmodule
